# Fritzing sketch pulse_ox (saved by Fritzing 0.9.9b)
breadboards: 2

parts:
  Part1 = Arduino Uno (Rev3)
  Power1 = PowerBRICK 12V
  LF412 = Dual Op-Amp [package=dip08]
  LF412_2 = Dual Op-Amp [package=dip08]
  LF412_3 = Dual Op-Amp [package=dip08]
  LF412_4 = Dual Op-Amp [package=dip08]
  LF398N = IC, DIP package, 8 pins [chip_label=IC]
  LF398N_2 = IC, DIP package, 8 pins [chip_label=IC]
  R1 = Resistor [tolerance=±5% resistance=220 package="2010 [SMD]"]
  R2 = Resistor [tolerance=±5% resistance=220 package="2010 [SMD]"]
  X1 = DB9 Connector [package=db9]
  R3 = Resistor [tolerance=±5% resistance=220 package="2010 [SMD]"]
  R4 = Resistor [tolerance=±5% resistance=330k package="2010 [SMD]"]
  C1 = Ceramic Capacitor [capacitance=1nF voltage=35V package="1206 [SMD, multilayer]"]
  R5 = Resistor [tolerance=±5% resistance=330k package="2010 [SMD]"]
  R6 = Resistor [tolerance=±5% resistance=330k package="2010 [SMD]"]
  C2 = Ceramic Capacitor [capacitance=0.1µF voltage=35V package="1206 [SMD, multilayer]"]
  C3 = Ceramic Capacitor [capacitance=0.1µF voltage=35V package="1206 [SMD, multilayer]"]
  C4 = Ceramic Capacitor [capacitance=0.1µF voltage=35V package="1206 [SMD, multilayer]"]
  C5 = Ceramic Capacitor [capacitance=1µF voltage=35V package="1206 [SMD, multilayer]"]
  R7 = Resistor [tolerance=±5% resistance=330k package="2010 [SMD]"]
  R8 = Resistor [tolerance=±5% resistance=330k package="2010 [SMD]"]
  R9 = Resistor [tolerance=±5% resistance=220 package="2010 [SMD]"]
  R10 = Resistor [tolerance=±5% resistance=220 package="2010 [SMD]"]
  R11 = Resistor [tolerance=±5% resistance=220 package="2010 [SMD]"]
  R12 = Resistor [tolerance=±5% resistance=220 package="2010 [SMD]"]
  R13 = Resistor [tolerance=±5% resistance=220 package="2010 [SMD]"]
  R14 = Resistor [tolerance=±5% resistance=220 package="2010 [SMD]"]
  C6 = Ceramic Capacitor [capacitance=1nF voltage=35V package="1206 [SMD, multilayer]"]
  R15 = Resistor [tolerance=±5% resistance=33k package="2010 [SMD]"]
  R16 = Resistor [tolerance=±5% resistance=33k package="2010 [SMD]"]
  C7 = Ceramic Capacitor [capacitance=1µF voltage=35V package="1206 [SMD, multilayer]"]
  C8 = Ceramic Capacitor [capacitance=1µF voltage=35V package="1206 [SMD, multilayer]"]
  C9 = Ceramic Capacitor [capacitance=1µF voltage=35V package="1206 [SMD, multilayer]"]
  C10 = Ceramic Capacitor [capacitance=1µF voltage=35V package="1206 [SMD, multilayer]"]
  R17 = Resistor [tolerance=±5% resistance=330k package="2010 [SMD]"]
  R18 = Resistor [tolerance=±5% resistance=330k package="2010 [SMD]"]
  R19 = Resistor [tolerance=±5% resistance=220 package="2010 [SMD]"]
  R20 = Resistor [tolerance=±5% resistance=220 package="2010 [SMD]"]
  R21 = Resistor [tolerance=±5% resistance=220 package="2010 [SMD]"]
  R22 = Resistor [tolerance=±5% resistance=220 package="2010 [SMD]"]
  R23 = Resistor [tolerance=±5% resistance=220 package="2010 [SMD]"]
  R24 = Resistor [tolerance=±5% resistance=220 package="2010 [SMD]"]

nets:
  N1: Part1.A0, LF398N.pin3, LF398N_2.pin2, X1.9, R4.Pin_1
  N2: Part1.A1, LF412_2.B_-IN, LF412_2.B_OUT, C3.0, C4.1
  N3: Part1.A2, LF412_4.B_-IN, LF412_4.B_OUT, C7.0, C10.1, R17.Pin_0
  N4: Part1.A3, LF412.B_OUT
  N5: Part1.A4/SDA, LF412_3.B_OUT, R23.Pin_1
  GND: Part1.GND, Power1.GND, R2.Pin_1, X1.5, X1.7, C1.1, C2.0, R8.Pin_0, R10.Pin_0, R14.Pin_0, C6.1, C8.1, R18.Pin_1, R20.Pin_1, R24.Pin_0
  N6: Part1.D2, R3.Pin_0
  N7: Part1.D3_PWM, LF398N.pin8, X1.2
  N8: Part1.5V, R1.Pin_0, R4.Pin_0, R12.Pin_1, R21.Pin_1
  N9: Power1.-Vout, LF412_2.A_V-, LF412_3.A_V-, LF412_4.A_+IN, LF398N.pin4, LF398N_2.pin4, C9.0, R18.Pin_0
  N10: Power1.+Vout, LF412.A_V-, LF412.A_V+, LF412_2.A_V+, LF412_3.B_-IN, LF398N.pin1, LF398N_2.pin1, R13.Pin_1, R23.Pin_0, R24.Pin_1
  N11: LF412.A_OUT, R9.Pin_1
  N12: LF412.A_-IN, R9.Pin_0, R10.Pin_1
  N13: LF412.A_+IN, LF412_2.A_OUT, LF412_2.A_-IN, R7.Pin_1
  N14: LF412.B_+IN, R11.Pin_0, R12.Pin_0
  N15: LF412.B_-IN, R13.Pin_0
  N16: LF412_2.A_+IN, C5.0, R8.Pin_1
  N17: LF412_2.B_+IN, R6.Pin_0, C2.1
  N18: LF412_3.A_OUT, R19.Pin_1, R22.Pin_1
  N19: LF412_3.A_-IN, R19.Pin_0
  N20: LF412_3.A_+IN, LF412_4.A_OUT, LF412_4.A_-IN, R17.Pin_1
  N21: LF412_3.B_+IN, R21.Pin_0, R22.Pin_0
  N22: LF412_4.B_+IN, C8.0
  N23: LF398N.pin5, R5.Pin_1
  N24: LF398N.pin6, C1.0
  N25: LF398N.pin7, LF398N_2.pin7, R1.Pin_1, R2.Pin_0
  N26: LF398N_2.pin6, C6.0
  N27: LF398N_2.pin8, X1.3, R3.Pin_1
  N28: R5.Pin_0, R6.Pin_1, C3.1
  N29: C4.0, C5.1, R7.Pin_0
  N30: R15.Pin_0, R16.Pin_1, C7.1
  N31: C9.1, C10.0

custom parts:
  PowerBRICK 12V: PowerBRICKs are split-rail power supply modules that are intended to be used with a breadboard. These generate both a negative and positive voltage out of a single 5V USB voltage.
  DB9 Connector: DB9 Connector Standard DB9 (D-Sub 9) serial connector. Can be used for CAN bus as well as RS485 and RS232. Footprint production proven. Spark Fun Electronics SKU : PRT-00429
